// Logisim project modular-sap-logisim.circ as structural Verilog: 2 circuits, main circuit main
module main (
  input  in_1,
  input  in_2,
  input  in_3,
  input  in_4,
  input  in_5,
  input  in_6,
  input  in_7,
  input  in_8,
  input  in_9,
  input  in_10,
  output out_11,
  output out_12,
  output out_13,
  output out_14,
  output out_15,
  output out_16,
  output out_17,
  output out_18
);

  wire clock_1_out;

  gp_reg gp_reg_1 (
    .out_12(out_11), .out_13(out_12), .out_14(out_13), .out_15(out_14), .out_16(out_15), .out_17(out_16),
    .out_18(out_17), .out_19(out_18), .in_1(in_1), .in_2(in_2), .in_3(in_3), .in_4(in_4), .in_5(in_5),
    .in_6(in_6), .in_7(in_7), .in_8(in_8), .in_9(clock_1_out), .in_10(in_9), .in_11(in_10));
  Clock clock_1 (.out(clock_1_out));
endmodule

module gp_reg (
  input  in_1,
  input  in_2,
  input  in_3,
  input  in_4,
  input  in_5,
  input  in_6,
  input  in_7,
  input  in_8,
  input  in_9,
  input  in_10,
  input  in_11,
  output out_12,
  output out_13,
  output out_14,
  output out_15,
  output out_16,
  output out_17,
  output out_18,
  output out_19
);

  wire d_ff_1_q, d_ff_2_q, d_ff_3_q, d_ff_4_q, d_ff_5_q, d_ff_6_q, d_ff_7_q, d_ff_8_q, multiplexer_1_out,
       multiplexer_2_out, multiplexer_3_out, multiplexer_4_out, multiplexer_5_out, multiplexer_6_out,
       multiplexer_7_out, multiplexer_8_out, not_1_out;

  not not_1 (not_1_out, in_10);
  Multiplexer #(.enable("false")) multiplexer_1 (.in0(in_1), .in1(d_ff_1_q), .out(multiplexer_1_out), .sel(not_1_out));
  D_Flip_Flop d_ff_1 (.clk(in_9), .D(multiplexer_1_out), .Q(d_ff_1_q));  // open: Qn, preset, reset
  assign out_12 = in_11 ? d_ff_1_q : 1'bz;  // Controlled_Buffer controlled_buffer_1
  Multiplexer #(.enable("false")) multiplexer_2 (.in0(in_2), .in1(d_ff_2_q), .out(multiplexer_2_out), .sel(not_1_out));
  D_Flip_Flop d_ff_2 (.clk(in_9), .D(multiplexer_2_out), .Q(d_ff_2_q));  // open: Qn, preset, reset
  Multiplexer #(.enable("false")) multiplexer_3 (.in0(in_3), .in1(d_ff_3_q), .out(multiplexer_3_out), .sel(not_1_out));
  assign out_13 = in_11 ? d_ff_2_q : 1'bz;  // Controlled_Buffer controlled_buffer_2
  Multiplexer #(.enable("false")) multiplexer_4 (.in0(in_4), .in1(d_ff_4_q), .out(multiplexer_4_out), .sel(not_1_out));
  D_Flip_Flop d_ff_3 (.clk(in_9), .D(multiplexer_3_out), .Q(d_ff_3_q));  // open: Qn, preset, reset
  assign out_14 = in_11 ? d_ff_3_q : 1'bz;  // Controlled_Buffer controlled_buffer_3
  D_Flip_Flop d_ff_4 (.clk(in_9), .D(multiplexer_4_out), .Q(d_ff_4_q));  // open: Qn, preset, reset
  assign out_15 = in_11 ? d_ff_4_q : 1'bz;  // Controlled_Buffer controlled_buffer_4
  Multiplexer #(.enable("false")) multiplexer_5 (.in0(in_5), .in1(d_ff_5_q), .out(multiplexer_5_out), .sel(not_1_out));
  Multiplexer #(.enable("false")) multiplexer_6 (.in0(in_6), .in1(d_ff_6_q), .out(multiplexer_6_out), .sel(not_1_out));
  D_Flip_Flop d_ff_5 (.clk(in_9), .D(multiplexer_5_out), .Q(d_ff_5_q));  // open: Qn, preset, reset
  assign out_16 = in_11 ? d_ff_5_q : 1'bz;  // Controlled_Buffer controlled_buffer_5
  D_Flip_Flop d_ff_6 (.clk(in_9), .D(multiplexer_6_out), .Q(d_ff_6_q));  // open: Qn, preset, reset
  assign out_17 = in_11 ? d_ff_6_q : 1'bz;  // Controlled_Buffer controlled_buffer_6
  Multiplexer #(.enable("false")) multiplexer_7 (.in0(in_7), .in1(d_ff_7_q), .out(multiplexer_7_out), .sel(not_1_out));
  D_Flip_Flop d_ff_7 (.clk(in_9), .D(multiplexer_7_out), .Q(d_ff_7_q));  // open: Qn, preset, reset
  assign out_18 = in_11 ? d_ff_7_q : 1'bz;  // Controlled_Buffer controlled_buffer_7
  Multiplexer #(.enable("false")) multiplexer_8 (.in0(in_8), .in1(d_ff_8_q), .out(multiplexer_8_out), .sel(not_1_out));
  D_Flip_Flop d_ff_8 (.clk(in_9), .D(multiplexer_8_out), .Q(d_ff_8_q));  // open: Qn, preset, reset
  assign out_19 = in_11 ? d_ff_8_q : 1'bz;  // Controlled_Buffer controlled_buffer_8
endmodule
