// Logisim project modular_sap.circ as structural Verilog: 7 circuits, main circuit main
module main (
);

  pc pc_1 ();  // open: pc_en, pc_clk, pc_reset, pc_out_en, pc_out
endmodule

module reg_gp (
  input  [7:0] reg_in,
  input  reg_in_en,
  input  reg_clk,
  input  reg_out_en,
  output [7:0] reg_int_out,
  output [7:0] reg_out
);

  wire multiplexer_1_out, multiplexer_2_out, multiplexer_3_out, multiplexer_4_out, multiplexer_5_out,
       multiplexer_6_out, multiplexer_7_out, multiplexer_8_out;

  Multiplexer multiplexer_1 (.in0(reg_int_out[7]), .in1(reg_in[7]), .out(multiplexer_1_out), .sel(reg_in_en));
  D_Flip_Flop d_ff_1 (.D(multiplexer_1_out), .clk(reg_clk), .Q(reg_int_out[7]));  // open: Qn, preset, reset
  assign reg_out[7] = reg_out_en ? reg_int_out[7] : 1'bz;  // Controlled_Buffer controlled_buffer_1
  Multiplexer multiplexer_2 (.in0(reg_int_out[6]), .in1(reg_in[6]), .out(multiplexer_2_out), .sel(reg_in_en));
  D_Flip_Flop d_ff_2 (.D(multiplexer_2_out), .clk(reg_clk), .Q(reg_int_out[6]));  // open: Qn, preset, reset
  Multiplexer multiplexer_3 (.in0(reg_int_out[5]), .in1(reg_in[5]), .out(multiplexer_3_out), .sel(reg_in_en));
  assign reg_out[6] = reg_out_en ? reg_int_out[6] : 1'bz;  // Controlled_Buffer controlled_buffer_2
  D_Flip_Flop d_ff_3 (.D(multiplexer_3_out), .clk(reg_clk), .Q(reg_int_out[5]));  // open: Qn, preset, reset
  Multiplexer multiplexer_4 (.in0(reg_int_out[4]), .in1(reg_in[4]), .out(multiplexer_4_out), .sel(reg_in_en));
  assign reg_out[5] = reg_out_en ? reg_int_out[5] : 1'bz;  // Controlled_Buffer controlled_buffer_3
  D_Flip_Flop d_ff_4 (.D(multiplexer_4_out), .clk(reg_clk), .Q(reg_int_out[4]));  // open: Qn, preset, reset
  Multiplexer multiplexer_5 (.in0(reg_int_out[3]), .in1(reg_in[3]), .out(multiplexer_5_out), .sel(reg_in_en));
  assign reg_out[4] = reg_out_en ? reg_int_out[4] : 1'bz;  // Controlled_Buffer controlled_buffer_4
  D_Flip_Flop d_ff_5 (.D(multiplexer_5_out), .clk(reg_clk), .Q(reg_int_out[3]));  // open: Qn, preset, reset
  Multiplexer multiplexer_6 (.in0(reg_int_out[2]), .in1(reg_in[2]), .out(multiplexer_6_out), .sel(reg_in_en));
  D_Flip_Flop d_ff_6 (.D(multiplexer_6_out), .clk(reg_clk), .Q(reg_int_out[2]));  // open: Qn, preset, reset
  assign reg_out[3] = reg_out_en ? reg_int_out[3] : 1'bz;  // Controlled_Buffer controlled_buffer_5
  assign reg_out[2] = reg_out_en ? reg_int_out[2] : 1'bz;  // Controlled_Buffer controlled_buffer_6
  Multiplexer multiplexer_7 (.in0(reg_int_out[1]), .in1(reg_in[1]), .out(multiplexer_7_out), .sel(reg_in_en));
  D_Flip_Flop d_ff_7 (.D(multiplexer_7_out), .clk(reg_clk), .Q(reg_int_out[1]));  // open: Qn, preset, reset
  assign reg_out[1] = reg_out_en ? reg_int_out[1] : 1'bz;  // Controlled_Buffer controlled_buffer_7
  Multiplexer multiplexer_8 (.in0(reg_int_out[0]), .in1(reg_in[0]), .out(multiplexer_8_out), .sel(reg_in_en));
  D_Flip_Flop d_ff_8 (.D(multiplexer_8_out), .clk(reg_clk), .Q(reg_int_out[0]));  // open: Qn, preset, reset
  assign reg_out[0] = reg_out_en ? reg_int_out[0] : 1'bz;  // Controlled_Buffer controlled_buffer_8

  // Notes on the sheet:
  //   Input
  //   Input Control
  //   Clock
  //   Output Control
  //   Memory
  //   Internal Output
  //   Output
endmodule

module alu (
  input  [7:0] alu_in_1,
  input  alu_out_en,
  input  alu_sub,
  input  [7:0] alu_in_2,
  output alu_carry_out,
  output [7:0] alu_out
);

  wire adder_2_cout, adder_3_cout, adder_4_cout, adder_5_cout, adder_6_cout, adder_7_cout, adder_8_cout,
       xor_1_out, xor_2_out, xor_3_out, xor_4_out, xor_5_out, xor_6_out, xor_7_out, xor_8_out;
  wire [7:0] adder_8_out;

  Adder #(.width(1)) adder_1 (
    .a(alu_in_1[7]), .b(xor_1_out), .out(adder_8_out[7]), .cin(adder_2_cout), .cout(alu_carry_out));
  xor xor_1 (xor_1_out, alu_in_2[7], alu_sub);
  Adder #(.width(1)) adder_2 (
    .a(alu_in_1[6]), .b(xor_2_out), .out(adder_8_out[6]), .cin(adder_3_cout), .cout(adder_2_cout));
  xor xor_2 (xor_2_out, alu_in_2[6], alu_sub);
  Adder #(.width(1)) adder_3 (
    .a(alu_in_1[5]), .b(xor_3_out), .out(adder_8_out[5]), .cin(adder_4_cout), .cout(adder_3_cout));
  xor xor_3 (xor_3_out, alu_in_2[5], alu_sub);
  Adder #(.width(1)) adder_4 (
    .a(alu_in_1[4]), .b(xor_4_out), .out(adder_8_out[4]), .cin(adder_5_cout), .cout(adder_4_cout));
  xor xor_4 (xor_4_out, alu_in_2[4], alu_sub);
  Adder #(.width(1)) adder_5 (
    .a(alu_in_1[3]), .b(xor_5_out), .out(adder_8_out[3]), .cin(adder_6_cout), .cout(adder_5_cout));
  xor xor_5 (xor_5_out, alu_in_2[3], alu_sub);
  Adder #(.width(1)) adder_6 (
    .a(alu_in_1[2]), .b(xor_6_out), .out(adder_8_out[2]), .cin(adder_7_cout), .cout(adder_6_cout));
  xor xor_6 (xor_6_out, alu_in_2[2], alu_sub);
  Adder #(.width(1)) adder_7 (
    .a(alu_in_1[1]), .b(xor_7_out), .out(adder_8_out[1]), .cin(adder_8_cout), .cout(adder_7_cout));
  xor xor_7 (xor_7_out, alu_in_2[1], alu_sub);
  Adder #(.width(1)) adder_8 (.a(alu_in_1[0]), .b(xor_8_out), .out(adder_8_out[0]), .cin(alu_sub), .cout(adder_8_cout));
  xor xor_8 (xor_8_out, alu_in_2[0], alu_sub);
  assign alu_out = alu_out_en ? adder_8_out : 8'bz;  // Controlled_Buffer controlled_buffer_1

  // Notes on the sheet:
  //   Input 1
  //   Carry Output
  //   Subtract Control
  //   Full Adders
  //   Input 2
  //   Output Control
  //   ALU Output
endmodule

module pc (
  input  pc_en,
  input  pc_clk,
  input  pc_reset,
  input  pc_out_en,
  output [3:0] pc_out
);

  wire j_k_ff_2_qn, j_k_ff_3_qn, j_k_ff_4_qn;
  wire [3:0] j_k_ff_4_q;

  J_K_Flip_Flop j_k_ff_1 (
    .J(pc_en), .K(pc_en), .clk(j_k_ff_2_qn), .Q(j_k_ff_4_q[3]), .reset(pc_reset));  // open: Qn, preset
  J_K_Flip_Flop j_k_ff_2 (
    .J(pc_en), .K(pc_en), .clk(j_k_ff_3_qn), .Q(j_k_ff_4_q[2]), .Qn(j_k_ff_2_qn), .reset(pc_reset));  // open: preset
  J_K_Flip_Flop j_k_ff_3 (
    .J(pc_en), .K(pc_en), .clk(j_k_ff_4_qn), .Q(j_k_ff_4_q[1]), .Qn(j_k_ff_3_qn), .reset(pc_reset));  // open: preset
  J_K_Flip_Flop j_k_ff_4 (
    .J(pc_en), .K(pc_en), .clk(pc_clk), .Q(j_k_ff_4_q[0]), .Qn(j_k_ff_4_qn), .reset(pc_reset));  // open: preset
  assign pc_out = pc_out_en ? j_k_ff_4_q : 4'bz;  // Controlled_Buffer controlled_buffer_1

  // Notes on the sheet:
  //   Clock
  //   Reset
  //   Output Control
  //   Count Control
  //   Counter Output
endmodule

module sram (
  input  [7:0] in_1
);

  wire [7:0] reg_gp_1_reg_int_out, reg_gp_2_reg_out, reg_gp_6_reg_out, reg_gp_10_reg_out, reg_gp_14_reg_out,
       undriven, undriven_2, undriven_3, undriven_4;

  reg_gp reg_gp_1 (.reg_in(in_1), .reg_int_out(reg_gp_1_reg_int_out));  // open: reg_in_en, reg_clk, reg_out_en, reg_out
  reg_gp reg_gp_2 (.reg_in(undriven), .reg_out(reg_gp_2_reg_out));  // open: reg_in_en, reg_clk, reg_out_en, reg_int_out
  reg_gp reg_gp_3 (.reg_in(undriven), .reg_out(reg_gp_2_reg_out));  // open: reg_in_en, reg_clk, reg_out_en, reg_int_out
  reg_gp reg_gp_4 (.reg_in(undriven), .reg_out(reg_gp_2_reg_out));  // open: reg_in_en, reg_clk, reg_out_en, reg_int_out
  reg_gp reg_gp_5 (.reg_in(undriven), .reg_out(reg_gp_2_reg_out));  // open: reg_in_en, reg_clk, reg_out_en, reg_int_out
  reg_gp reg_gp_6 (
    .reg_in(undriven_2), .reg_out(reg_gp_6_reg_out));  // open: reg_in_en, reg_clk, reg_out_en, reg_int_out
  reg_gp reg_gp_7 (
    .reg_in(undriven_2), .reg_out(reg_gp_6_reg_out));  // open: reg_in_en, reg_clk, reg_out_en, reg_int_out
  reg_gp reg_gp_8 (
    .reg_in(undriven_2), .reg_out(reg_gp_6_reg_out));  // open: reg_in_en, reg_clk, reg_out_en, reg_int_out
  reg_gp reg_gp_9 (
    .reg_in(undriven_2), .reg_out(reg_gp_6_reg_out));  // open: reg_in_en, reg_clk, reg_out_en, reg_int_out
  reg_gp reg_gp_10 (
    .reg_in(undriven_3), .reg_out(reg_gp_10_reg_out));  // open: reg_in_en, reg_clk, reg_out_en, reg_int_out
  reg_gp reg_gp_11 (
    .reg_in(undriven_3), .reg_out(reg_gp_10_reg_out));  // open: reg_in_en, reg_clk, reg_out_en, reg_int_out
  reg_gp reg_gp_12 (
    .reg_in(undriven_3), .reg_out(reg_gp_10_reg_out));  // open: reg_in_en, reg_clk, reg_out_en, reg_int_out
  reg_gp reg_gp_13 (
    .reg_in(undriven_3), .reg_out(reg_gp_10_reg_out));  // open: reg_in_en, reg_clk, reg_out_en, reg_int_out
  reg_gp reg_gp_14 (
    .reg_in(undriven_4), .reg_out(reg_gp_14_reg_out));  // open: reg_in_en, reg_clk, reg_out_en, reg_int_out
  reg_gp reg_gp_15 (
    .reg_in(undriven_4), .reg_out(reg_gp_14_reg_out));  // open: reg_in_en, reg_clk, reg_out_en, reg_int_out
  reg_gp reg_gp_16 (
    .reg_in(undriven_4), .reg_out(reg_gp_14_reg_out));  // open: reg_in_en, reg_clk, reg_out_en, reg_int_out
  reg_gp reg_gp_17 (
    .reg_in(undriven_4), .reg_out(reg_gp_14_reg_out));  // open: reg_in_en, reg_clk, reg_out_en, reg_int_out
endmodule

module dec_4x16 (
  input  [3:0] dec_sel,
  output [15:0] out_2
);

  wire not_1_out, not_2_out, not_3_out, not_4_out;

  not not_1 (not_1_out, dec_sel[3]);
  not not_2 (not_2_out, dec_sel[2]);
  not not_3 (not_3_out, dec_sel[1]);
  not not_4 (not_4_out, dec_sel[0]);
  and and_1 (out_2[0], not_4_out, not_3_out, not_2_out, not_1_out);
  and and_2 (out_2[1], dec_sel[0], not_3_out, not_2_out, not_1_out);
  and and_3 (out_2[2], not_4_out, dec_sel[1], not_2_out, not_1_out);
  and and_4 (out_2[3], dec_sel[0], dec_sel[1], not_2_out, not_1_out);
  and and_5 (out_2[4], not_4_out, not_3_out, dec_sel[2], not_1_out);
  and and_6 (out_2[5], dec_sel[0], not_3_out, dec_sel[2], not_1_out);
  and and_7 (out_2[6], not_4_out, dec_sel[1], dec_sel[2], not_1_out);
  and and_8 (out_2[7], dec_sel[0], dec_sel[1], dec_sel[2], not_1_out);
  and and_9 (out_2[8], not_4_out, not_3_out, not_2_out, dec_sel[3]);
  and and_10 (out_2[9], dec_sel[0], not_3_out, not_2_out, dec_sel[3]);
  and and_11 (out_2[10], not_4_out, dec_sel[1], not_2_out, dec_sel[3]);
  and and_12 (out_2[11], dec_sel[0], dec_sel[1], not_2_out, dec_sel[3]);
  and and_13 (out_2[12], not_4_out, not_3_out, dec_sel[2], dec_sel[3]);
  and and_14 (out_2[13], dec_sel[0], not_3_out, dec_sel[2], dec_sel[3]);
  and and_15 (out_2[14], not_4_out, dec_sel[1], dec_sel[2], dec_sel[3]);
  and and_16 (out_2[15], dec_sel[0], dec_sel[1], dec_sel[2], dec_sel[3]);
endmodule

module sram_cell (
);

  reg_gp reg_gp_1 ();  // open: reg_in, reg_in_en, reg_clk, reg_out_en, reg_int_out, reg_out
endmodule
